// Logisim project task3.circ as structural Verilog: 2 circuits, main circuit main
module main (
  output [7:0] out_1
);

  wire clock_1_out;

  Clock clock_1 (.out(clock_1_out));
  my_counter my_counter_1 (.clk(clock_1_out), .Q(out_1));  // open: reset
endmodule

module my_counter (
  input  clk,
  input  reset,
  output [7:0] Q
);

  wire adder_1_cout;
  wire [7:0] register_1_q;

  Adder adder_1 (.a(register_1_q), .b(8'h1), .out(Q), .cin(1'b0), .cout(adder_1_cout));
  Register register_1 (.D(Q), .en(1'b1), .clk(clk), .Q(register_1_q), .clr(reset));
  // also tied to GND on the sheet: adder_1_cout
endmodule
